// Logisim project First assignment.circ as structural Verilog: 1 circuit, main circuit main
module main (
  input  in_1,
  input  in_2,
  input  in_3,
  input  in_4,
  output out_5
);

  wire or_1_out, undriven;

  or or_1 (or_1_out, in_1, undriven, in_3);
  and and_1 (out_5, or_1_out, in_4);
endmodule
