// Logisim project Third assignment.circ as structural Verilog: 1 circuit, main circuit main
module main (
  input  in_1,
  input  in_2,
  input  in_3,
  output out_4
);

  wire and_1_out, and_2_out, nor_1_out, nor_2_out, or_1_out;

  nor nor_1 (nor_1_out, in_2, in_3);
  and and_1 (and_1_out, in_2, in_3);
  or or_1 (or_1_out, nor_1_out, and_1_out);
  and and_2 (and_2_out, in_1, or_1_out);
  nor nor_2 (nor_2_out, in_1, or_1_out);
  nor nor_3 (out_4, and_2_out, nor_2_out);
endmodule
