// Logisim project a limited ALU.circ as structural Verilog: 1 circuit, main circuit main
module main (
  input  [3:0] in_1,
  input  in_2,
  input  [3:0] in_3,
  input  [1:0] _01____subtractor,
  output [3:0] out_5,
  output Overflow,
  output Overflow_2
);

  wire and_1_out, and_2_out, and_3_out, and_4_out, and_5_out, and_6_out, and_7_out, and_8_out, and_9_out,
       and_10_out, and_11_out, and_12_out, and_13_out, and_14_out, and_15_out, and_16_out, and_17_out,
       and_18_out, and_19_out, and_20_out, and_21_out, and_22_out, and_23_out, and_24_out, and_25_out,
       and_26_out, and_27_out, and_28_out, and_29_out, and_30_out, and_31_out, and_32_out, and_33_out,
       and_34_out, and_35_out, and_36_out, and_37_out, and_38_out, and_39_out, and_40_out, and_41_out,
       and_42_out, and_43_out, and_44_out, and_45_out, and_46_out, and_47_out, and_48_out, and_49_out,
       and_50_out, and_51_out, and_52_out, and_53_out, and_54_out, and_55_out, and_56_out, clock_1_out,
       clock_2_out, d_ff_1_q, d_ff_2_q, d_ff_3_q, d_ff_4_q, d_ff_5_q, d_ff_6_q, d_ff_7_q, d_ff_8_q,
       not_1_out, not_2_out, not_3_out, not_4_out, or_2_out, or_4_out, or_6_out, or_14_out, or_16_out,
       or_18_out;
  wire [3:0] and_57_out, or_1_out, or_9_out, or_13_out;

  Clock clock_1 (.out(clock_1_out));
  Clock clock_2 (.out(clock_2_out));
  D_Flip_Flop d_ff_1 (.clk(clock_1_out), .D(in_1[3]), .Q(d_ff_1_q));  // open: Qn, preset, en, reset
  D_Flip_Flop d_ff_2 (.clk(clock_2_out), .D(in_3[3]), .Q(d_ff_2_q));  // open: Qn, preset, en, reset
  D_Flip_Flop d_ff_3 (.clk(clock_1_out), .D(in_1[2]), .Q(d_ff_3_q));  // open: Qn, preset, en, reset
  D_Flip_Flop d_ff_4 (.clk(clock_2_out), .D(in_3[2]), .Q(d_ff_4_q));  // open: Qn, preset, en, reset
  D_Flip_Flop d_ff_5 (.clk(clock_1_out), .D(in_1[1]), .Q(d_ff_5_q));  // open: Qn, preset, en, reset
  D_Flip_Flop d_ff_6 (.clk(clock_2_out), .D(in_3[1]), .Q(d_ff_6_q));  // open: Qn, preset, en, reset
  D_Flip_Flop d_ff_7 (.clk(clock_1_out), .D(in_1[0]), .Q(d_ff_7_q));  // open: Qn, preset, en, reset
  D_Flip_Flop d_ff_8 (.clk(clock_2_out), .D(in_3[0]), .Q(d_ff_8_q));  // open: Qn, preset, en, reset
  not not_1 (not_1_out, d_ff_8_q);
  not not_2 (not_2_out, d_ff_6_q);
  not not_3 (not_3_out, d_ff_4_q);
  not not_4 (not_4_out, d_ff_2_q);
  and and_1 (and_1_out, ~d_ff_7_q, ~d_ff_8_q, in_2);  // AND_Gate
  and and_2 (and_2_out, d_ff_7_q, ~d_ff_8_q, ~in_2);  // AND_Gate
  and and_3 (and_3_out, ~d_ff_7_q, d_ff_8_q, ~in_2);  // AND_Gate
  and and_4 (and_4_out, d_ff_7_q, d_ff_8_q, in_2);
  and and_5 (and_5_out, d_ff_7_q, d_ff_8_q);
  and and_6 (and_6_out, d_ff_7_q, in_2);
  and and_7 (and_7_out, in_2, d_ff_8_q);
  and and_8 (and_8_out, ~d_ff_5_q, ~d_ff_6_q, or_2_out);  // AND_Gate
  and and_9 (and_9_out, d_ff_5_q, ~d_ff_6_q, ~or_2_out);  // AND_Gate
  and and_10 (and_10_out, ~d_ff_5_q, d_ff_6_q, ~or_2_out);  // AND_Gate
  and and_11 (and_11_out, d_ff_5_q, d_ff_6_q, or_2_out);
  and and_12 (and_12_out, d_ff_5_q, d_ff_6_q);
  and and_13 (and_13_out, d_ff_5_q, or_2_out);
  and and_14 (and_14_out, or_2_out, d_ff_6_q);
  and and_15 (and_15_out, ~d_ff_3_q, ~d_ff_4_q, or_4_out);  // AND_Gate
  and and_16 (and_16_out, d_ff_3_q, ~d_ff_4_q, ~or_4_out);  // AND_Gate
  and and_17 (and_17_out, ~d_ff_3_q, d_ff_4_q, ~or_4_out);  // AND_Gate
  and and_18 (and_18_out, d_ff_3_q, d_ff_4_q, or_4_out);
  and and_19 (and_19_out, d_ff_3_q, d_ff_4_q);
  and and_20 (and_20_out, d_ff_3_q, or_4_out);
  and and_21 (and_21_out, or_4_out, d_ff_4_q);
  and and_22 (and_22_out, ~d_ff_1_q, ~d_ff_2_q, or_6_out);  // AND_Gate
  and and_23 (and_23_out, d_ff_1_q, ~d_ff_2_q, ~or_6_out);  // AND_Gate
  and and_24 (and_24_out, ~d_ff_1_q, d_ff_2_q, ~or_6_out);  // AND_Gate
  and and_25 (and_25_out, d_ff_1_q, d_ff_2_q, or_6_out);
  and and_26 (and_26_out, d_ff_1_q, d_ff_2_q);
  and and_27 (and_27_out, d_ff_1_q, or_6_out);
  and and_28 (and_28_out, or_6_out, d_ff_2_q);
  or or_1 (or_1_out[0], and_1_out, and_2_out, and_3_out, and_4_out);
  or or_2 (or_2_out, and_5_out, and_6_out, and_7_out);
  or or_3 (or_1_out[1], and_8_out, and_9_out, and_10_out, and_11_out);
  or or_4 (or_4_out, and_12_out, and_13_out, and_14_out);
  or or_5 (or_1_out[2], and_15_out, and_16_out, and_17_out, and_18_out);
  or or_6 (or_6_out, and_19_out, and_20_out, and_21_out);
  or or_7 (or_1_out[3], and_22_out, and_23_out, and_24_out, and_25_out);
  or or_8 (Overflow, and_26_out, and_27_out, and_28_out);
  and and_29 (and_29_out, ~d_ff_7_q, ~not_1_out, 1'b1);  // AND_Gate
  and and_30 (and_30_out, d_ff_7_q, ~not_1_out, ~1'b1);  // AND_Gate
  and and_31 (and_31_out, ~d_ff_7_q, not_1_out, ~1'b1);  // AND_Gate
  and and_32 (and_32_out, d_ff_7_q, not_1_out, 1'b1);
  and and_33 (and_33_out, d_ff_7_q, not_1_out);
  and and_34 (and_34_out, d_ff_7_q, 1'b1);
  and and_35 (and_35_out, 1'b1, not_1_out);
  and and_36 (and_36_out, ~d_ff_5_q, ~not_2_out, or_14_out);  // AND_Gate
  and and_37 (and_37_out, d_ff_5_q, ~not_2_out, ~or_14_out);  // AND_Gate
  and and_38 (and_38_out, ~d_ff_5_q, not_2_out, ~or_14_out);  // AND_Gate
  and and_39 (and_39_out, d_ff_5_q, not_2_out, or_14_out);
  and and_40 (and_40_out, d_ff_5_q, not_2_out);
  and and_41 (and_41_out, d_ff_5_q, or_14_out);
  and and_42 (and_42_out, or_14_out, not_2_out);
  and and_43 (and_43_out, ~d_ff_3_q, ~not_3_out, or_16_out);  // AND_Gate
  and and_44 (and_44_out, d_ff_3_q, ~not_3_out, ~or_16_out);  // AND_Gate
  and and_45 (and_45_out, ~d_ff_3_q, not_3_out, ~or_16_out);  // AND_Gate
  and and_46 (and_46_out, d_ff_3_q, not_3_out, or_16_out);
  and and_47 (and_47_out, d_ff_3_q, not_3_out);
  and and_48 (and_48_out, d_ff_3_q, or_16_out);
  and and_49 (and_49_out, or_16_out, not_3_out);
  and and_50 (and_50_out, ~d_ff_1_q, ~not_4_out, or_18_out);  // AND_Gate
  and and_51 (and_51_out, d_ff_1_q, ~not_4_out, ~or_18_out);  // AND_Gate
  and and_52 (and_52_out, ~d_ff_1_q, not_4_out, ~or_18_out);  // AND_Gate
  and and_53 (and_53_out, d_ff_1_q, not_4_out, or_18_out);
  and and_54 (and_54_out, d_ff_1_q, not_4_out);
  and and_55 (and_55_out, d_ff_1_q, or_18_out);
  and and_56 (and_56_out, or_18_out, not_4_out);
  and and_57 (and_57_out[0], d_ff_7_q, d_ff_8_q);
  and and_58 (and_57_out[1], d_ff_5_q, d_ff_6_q);
  and and_59 (and_57_out[2], d_ff_3_q, d_ff_4_q);
  and and_60 (and_57_out[3], d_ff_1_q, d_ff_2_q);
  or or_9 (or_9_out[0], d_ff_7_q, d_ff_8_q);
  or or_10 (or_9_out[1], d_ff_5_q, d_ff_6_q);
  or or_11 (or_9_out[2], d_ff_3_q, d_ff_4_q);
  or or_12 (or_9_out[3], d_ff_1_q, d_ff_2_q);
  or or_13 (or_13_out[0], and_29_out, and_30_out, and_31_out, and_32_out);
  or or_14 (or_14_out, and_33_out, and_34_out, and_35_out);
  or or_15 (or_13_out[1], and_36_out, and_37_out, and_38_out, and_39_out);
  or or_16 (or_16_out, and_40_out, and_41_out, and_42_out);
  or or_17 (or_13_out[2], and_43_out, and_44_out, and_45_out, and_46_out);
  or or_18 (or_18_out, and_47_out, and_48_out, and_49_out);
  or or_19 (or_13_out[3], and_50_out, and_51_out, and_52_out, and_53_out);
  or or_20 (Overflow_2, and_54_out, and_55_out, and_56_out);
  Multiplexer #(.select(2), .width(4)) multiplexer_1 (
    .in0(or_1_out), .in1(or_13_out), .in2(and_57_out), .in3(or_9_out), .out(out_5), .sel(_01____subtractor));  // open: en

  // Notes on the sheet:
  //   First 4-bit binary number
  //   CONTROL (ENABLE)
  //   Second 4-bit binary number
  //   CONTROL (ENABLE)
  //   00 -> adder
  //   10 -> bitwise AND
  //   11 -> bitwise OR
endmodule
