// Logisim project two 4-bit binary subtractor.circ as structural Verilog: 1 circuit, main circuit main
module main (
  input  [3:0] in_1,
  input  [3:0] in_2,
  output [3:0] out_3,
  output Overflow
);

  wire and_1_out, and_2_out, and_3_out, and_4_out, and_5_out, and_6_out, and_7_out, and_8_out, and_9_out,
       and_10_out, and_11_out, and_12_out, and_13_out, and_14_out, and_15_out, and_16_out, and_17_out,
       and_18_out, and_19_out, and_20_out, and_21_out, and_22_out, and_23_out, and_24_out, and_25_out,
       and_26_out, and_27_out, and_28_out, not_1_out, not_2_out, not_3_out, not_4_out, or_2_out, or_4_out,
       or_6_out;

  not not_1 (not_1_out, in_2[0]);
  not not_2 (not_2_out, in_2[1]);
  not not_3 (not_3_out, in_2[2]);
  not not_4 (not_4_out, in_2[3]);
  and and_1 (and_1_out, ~in_1[0], ~not_1_out, 1'b1);  // AND_Gate
  and and_2 (and_2_out, in_1[0], ~not_1_out, ~1'b1);  // AND_Gate
  and and_3 (and_3_out, ~in_1[0], not_1_out, ~1'b1);  // AND_Gate
  and and_4 (and_4_out, in_1[0], not_1_out, 1'b1);
  and and_5 (and_5_out, in_1[0], not_1_out);
  and and_6 (and_6_out, in_1[0], 1'b1);
  and and_7 (and_7_out, 1'b1, not_1_out);
  and and_8 (and_8_out, ~in_1[1], ~not_2_out, or_2_out);  // AND_Gate
  and and_9 (and_9_out, in_1[1], ~not_2_out, ~or_2_out);  // AND_Gate
  and and_10 (and_10_out, ~in_1[1], not_2_out, ~or_2_out);  // AND_Gate
  and and_11 (and_11_out, in_1[1], not_2_out, or_2_out);
  and and_12 (and_12_out, in_1[1], not_2_out);
  and and_13 (and_13_out, in_1[1], or_2_out);
  and and_14 (and_14_out, or_2_out, not_2_out);
  and and_15 (and_15_out, ~in_1[2], ~not_3_out, or_4_out);  // AND_Gate
  and and_16 (and_16_out, in_1[2], ~not_3_out, ~or_4_out);  // AND_Gate
  and and_17 (and_17_out, ~in_1[2], not_3_out, ~or_4_out);  // AND_Gate
  and and_18 (and_18_out, in_1[2], not_3_out, or_4_out);
  and and_19 (and_19_out, in_1[2], not_3_out);
  and and_20 (and_20_out, in_1[2], or_4_out);
  and and_21 (and_21_out, or_4_out, not_3_out);
  and and_22 (and_22_out, ~in_1[3], ~not_4_out, or_6_out);  // AND_Gate
  and and_23 (and_23_out, in_1[3], ~not_4_out, ~or_6_out);  // AND_Gate
  and and_24 (and_24_out, ~in_1[3], not_4_out, ~or_6_out);  // AND_Gate
  and and_25 (and_25_out, in_1[3], not_4_out, or_6_out);
  and and_26 (and_26_out, in_1[3], not_4_out);
  and and_27 (and_27_out, in_1[3], or_6_out);
  and and_28 (and_28_out, or_6_out, not_4_out);
  or or_1 (out_3[0], and_1_out, and_2_out, and_3_out, and_4_out);
  or or_2 (or_2_out, and_5_out, and_6_out, and_7_out);
  or or_3 (out_3[1], and_8_out, and_9_out, and_10_out, and_11_out);
  or or_4 (or_4_out, and_12_out, and_13_out, and_14_out);
  or or_5 (out_3[2], and_15_out, and_16_out, and_17_out, and_18_out);
  or or_6 (or_6_out, and_19_out, and_20_out, and_21_out);
  or or_7 (out_3[3], and_22_out, and_23_out, and_24_out, and_25_out);
  or or_8 (Overflow, and_26_out, and_27_out, and_28_out);

  // Notes on the sheet:
  //   Second 4-bit number to be subtracted
  //   First 4-bit binary number
  //   Output of subtractor
endmodule
