// Logisim project memory register capable of storing 4 bit.circ as structural Verilog: 1 circuit, main circuit main
module main (
  input  D3,
  input  D2,
  input  D1,
  input  D0,
  output Q3,
  output Q2,
  output Q1,
  output Q0
);

  wire clock_1_out;

  Clock clock_1 (.out(clock_1_out));
  D_Flip_Flop d_ff_1 (.clk(clock_1_out), .D(D3), .Q(Q3));  // open: Qn, preset, en, reset
  D_Flip_Flop d_ff_2 (.clk(clock_1_out), .D(D2), .Q(Q2));  // open: Qn, preset, en, reset
  D_Flip_Flop d_ff_3 (.clk(clock_1_out), .D(D1), .Q(Q1));  // open: Qn, preset, en, reset
  D_Flip_Flop d_ff_4 (.clk(clock_1_out), .D(D0), .Q(Q0));  // open: Qn, preset, en, reset

  // Notes on the sheet:
  //   CONTROL (ENABLE)
endmodule
